# Fritzing sketch IrrigationCircuit (saved by Fritzing 1.0.7)
circuit board: 8.46667cm x 8cm
stripboards: 6

parts:
  T1 = Pushbutton [package=THT]
  T2 = Pushbutton [package=THT]
  T3 = Pushbutton [package=THT]
  T4 = Pushbutton [package=THT]
  T5 = Pushbutton [package=THT]
  T6 = Pushbutton [package=THT]
  T7 = Pushbutton [package=THT]
  T8 = Pushbutton [package=THT]
  T9 = Pushbutton [package=THT]
  A1 = ESP32 DevKitc V4
  R6 = Resistor [tolerance=±5% power=0.25W resistance=10k package=THT]
  R7 = Resistor [tolerance=±5% power=0.25W resistance=10k package=THT]
  R8 = Resistor [tolerance=±5% power=0.25W resistance=10k package=THT]
  A2 = AZDelivery 2channel solid state relay module
  A3 = AZDelivery 2channel solid state relay module
  A4 = AZDelivery 2channel solid state relay module
  A5 = AZDelivery 2channel solid state relay module
  A6 = AZDelivery 2channel solid state relay module
  LED1 = LED - 5mm [color="Red (633nm)" current=0.030A package="5 mm [THT]"]
  V1 = Inductor [inductance=0H package="400 mil [THT]"]
  V2 = Inductor [inductance=0H package="400 mil [THT]"]
  V3 = Inductor [inductance=0H package="400 mil [THT]"]
  V4 = Inductor [inductance=0H package="400 mil [THT]"]
  V5 = Inductor [inductance=0H package="400 mil [THT]"]
  V6 = Inductor [inductance=0H package="400 mil [THT]"]
  V7 = Inductor [inductance=0H package="400 mil [THT]"]
  V8 = Inductor [inductance=0H package="400 mil [THT]"]
  V9 = Inductor [inductance=0H package="400 mil [THT]"]
  D1 = Rectifier Diode [part_number=1N4001 package="300 mil [THT]"]
  R9 = Resistor [tolerance=±5% power=0.25W resistance=10k package=THT]
  J1 = screw terminal, 3 pins
  LED2 = LED - 5mm [color="Red (633nm)" current=0.030A package="5 mm [THT]"]
  J2 = screw terminal, 3 pins
  D2 = Rectifier Diode [part_number=1N4001 package="300 mil [THT]"]
  R10 = Resistor [tolerance=±5% power=0.25W resistance=10k package=THT]
  D3 = Rectifier Diode [part_number=1N4001 package="300 mil [THT]"]
  R11 = Resistor [tolerance=±5% power=0.25W resistance=10k package=THT]
  J3 = screw terminal, 3 pins
  LED3 = LED - 5mm [color="Red (633nm)" current=0.030A package="5 mm [THT]"]
  D4 = Rectifier Diode [part_number=1N4001 package="300 mil [THT]"]
  R12 = Resistor [tolerance=±5% power=0.25W resistance=10k package=THT]
  J4 = screw terminal, 3 pins
  LED4 = LED - 5mm [color="Red (633nm)" current=0.030A package="5 mm [THT]"]
  D5 = Rectifier Diode [part_number=1N4001 package="300 mil [THT]"]
  R13 = Resistor [tolerance=±5% power=0.25W resistance=10k package=THT]
  J5 = screw terminal, 3 pins
  LED5 = LED - 5mm [color="Red (633nm)" current=0.030A package="5 mm [THT]"]
  D6 = Rectifier Diode [part_number=1N4001 package="300 mil [THT]"]
  R14 = Resistor [tolerance=±5% power=0.25W resistance=10k package=THT]
  J6 = screw terminal, 3 pins
  LED6 = LED - 5mm [color="Red (633nm)" current=0.030A package="5 mm [THT]"]
  D7 = Rectifier Diode [part_number=1N4001 package="300 mil [THT]"]
  D8 = Rectifier Diode [part_number=1N4001 package="300 mil [THT]"]
  D9 = Rectifier Diode [part_number=1N4001 package="300 mil [THT]"]
  R15 = Resistor [tolerance=±5% power=0.25W resistance=10k package=THT]
  R16 = Resistor [tolerance=±5% power=0.25W resistance=10k package=THT]
  R17 = Resistor [tolerance=±5% power=0.25W resistance=10k package=THT]
  J7 = screw terminal, 3 pins
  J8 = screw terminal, 3 pins
  J9 = screw terminal, 3 pins
  LED7 = LED - 5mm [color="Red (633nm)" current=0.030A package="5 mm [THT]"]
  LED8 = LED - 5mm [color="Red (633nm)" current=0.030A package="5 mm [THT]"]
  LED9 = LED - 5mm [color="Red (633nm)" current=0.030A package="5 mm [THT]"]

nets:
  N1: T1.leg0, A1.Pin_26
  N2: T1.leg1, T2.leg1, T3.leg1, T4.leg1, T5.leg1, T6.leg1, T7.leg1, T8.leg1, T9.leg1, A1.Pin_1
  N3: T2.leg0, A1.Pin_15
  N4: T3.leg0, A1.Pin_12
  N5: T4.leg0, A1.Pin_11
  N6: T5.leg0, A1.Pin_7
  N7: T6.leg0, A1.Pin_8
  N8: T7.leg0, A1.Pin_5, R7.Pin_1
  N9: T8.leg0, A1.Pin_6, R6.Pin_1
  N10: T9.leg0, A1.Pin_4, R8.Pin_1
  N11: A1.Pin_9, A3.Pin_4
  N12: A1.Pin_10, A2.Pin_3
  N13: A1.Pin_14, A1.Pin_32, A1.Pin_38, R6.Pin_0, R7.Pin_0, R8.Pin_0
  N14: A1.Pin_27, A6.Pin_3
  N15: A1.Pin_28, A6.Pin_4
  N16: A1.Pin_30, A5.Pin_3
  N17: A1.Pin_31, A5.Pin_4
  N18: A1.Pin_33, A4.Pin_3
  N19: A1.Pin_36, A4.Pin_4
  N20: A1.Pin_37, A3.Pin_3
  N21: A2.Pin_7, V9.pin_1
  N22: A2.Pin_8, A3.Pin_6, A3.Pin_8, A4.Pin_6, A4.Pin_8, A5.Pin_6, A5.Pin_8, A6.Pin_6, A6.Pin_8
  N23: A3.Pin_5, V8.pin_1
  N24: A3.Pin_7, V7.pin_1
  N25: A4.Pin_5, V6.pin_1
  N26: A4.Pin_7, V5.pin_1
  N27: A5.Pin_5, V4.pin_1
  N28: A5.Pin_7, V3.pin_1
  N29: A6.Pin_5, V2.pin_1
  N30: A6.Pin_7, V1.pin_1
  N31: LED1.cathode, D1.anode, J1.pin3
  N32: LED1.anode, D1.cathode, R9.Pin_1, J1.pin2
  N33: V1.pin_0, V2.pin_0, V3.pin_0, V4.pin_0, V5.pin_0, V6.pin_0, V7.pin_0, V8.pin_0, V9.pin_0
  N34: R9.Pin_0, J1.pin1
  N35: LED2.cathode, J2.pin3, D2.anode
  N36: LED2.anode, J2.pin2, D2.cathode, R10.Pin_1
  N37: J2.pin1, R10.Pin_0
  N38: D3.cathode, R11.Pin_1, J3.pin2, LED3.anode
  N39: D3.anode, J3.pin3, LED3.cathode
  N40: R11.Pin_0, J3.pin1
  N41: D4.cathode, R12.Pin_1, J4.pin2, LED4.anode
  N42: D4.anode, J4.pin3, LED4.cathode
  N43: R12.Pin_0, J4.pin1
  N44: D5.cathode, R13.Pin_1, J5.pin2, LED5.anode
  N45: D5.anode, J5.pin3, LED5.cathode
  N46: R13.Pin_0, J5.pin1
  N47: D6.cathode, R14.Pin_1, J6.pin2, LED6.anode
  N48: D6.anode, J6.pin3, LED6.cathode
  N49: R14.Pin_0, J6.pin1
  N50: D7.cathode, R17.Pin_1, J7.pin2, LED8.anode
  N51: D7.anode, J7.pin3, LED8.cathode
  N52: D8.cathode, R16.Pin_1, J9.pin2, LED7.anode
  N53: D8.anode, J9.pin3, LED7.cathode
  N54: D9.cathode, R15.Pin_1, J8.pin2, LED9.anode
  N55: D9.anode, J8.pin3, LED9.cathode
  N56: R15.Pin_0, J8.pin1
  N57: R16.Pin_0, J9.pin1
  N58: R17.Pin_0, J7.pin1

notes:
  24 V AC
  5 V DC

custom parts:
  ESP32 DevKitc V4: ESP32-DevKitC board with ESP32-WROOM-32 module. ESP32-DevKitC V4 is a small-sized ESP32-based development board produced by Espressif. Most of the pins on the ESP module are broken out to the pin headers on the board. The pins D0, D1, D2, D3, CMD and CLK are used internally for communication between ESP32 and SPI flash memory. They are grouped on both sides near the USB connector. Avoid using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
  AZDelivery 2channel solid state relay module: AZDelivery 2channel solid state relay module.
